// Digital circuit solucio.dig as structural Verilog
module solucio (
  input  A0,
  input  A1,
  input  A2,
  input  A3,
  input  B0,
  input  B1,
  input  B2,
  input  B3,
  output R0,
  output R1,
  output R2
);

  wire alu_1_ovf;

  ALU alu_1 (
    .A0(A0), .A1(A1), .A2(A2), .B0(A3), .B1(B0), .B2(B1), .C0(B2), .C1(B3), .R0(R0), .R1(R1), .R2(R2),
    .OVF(alu_1_ovf));
  LED OVF (.in(alu_1_ovf));
endmodule
